// Logisim project latch and flip-flop.circ as structural Verilog: 1 circuit, main circuit main
module main (
  input  R,
  input  S,
  input  Enable,
  input  R_2,
  input  S_2,
  input  S_3,
  input  S_4,
  input  R_3,
  input  R_4,
  input  D,
  input  D_2,
  input  J,
  input  J_2,
  input  K,
  input  K_2,
  input  T,
  input  T_2,
  output Q,
  output Q_2,
  output nQ,
  output nQ_2,
  output Q_3,
  output Q_4,
  output nQ_3,
  output nQ_4,
  output Q_5,
  output Q_6,
  output nQ_5,
  output nQ_6,
  output Q_7,
  output Q_8,
  output nQ_7,
  output nQ_8,
  output Q_9,
  output Q_10,
  output nQ_9,
  output nQ_10
);

  wire clock_1_out, clock_2_out, clock_3_out, clock_4_out, clock_5_out, clock_6_out, clock_7_out,
       clock_8_out, nand_1_out, nand_2_out;

  Clock clock_1 (.out(clock_1_out));
  Clock clock_2 (.out(clock_2_out));
  Clock clock_3 (.out(clock_3_out));
  Clock clock_4 (.out(clock_4_out));
  nor G1 (Q, R, nQ_2);
  nor G1_2 (nQ_2, Q, S_2);
  S_R_Flip_Flop SR_F_F_Rising (.S(S_3), .clk(clock_1_out), .R(R_3), .Q(Q_3), .Qn(nQ_3));  // open: preset, reset, en
  D_Flip_Flop D_F_F_Rising (.clk(clock_2_out), .D(D_2), .Q(Q_6), .Qn(nQ_6));  // open: preset, en, reset
  J_K_Flip_Flop JK_F_F_Rising (.J(J), .clk(clock_3_out), .K(K), .Q(Q_7), .Qn(nQ_7));  // open: preset, en, reset
  T_Flip_Flop T_F_F_Rising (.clk(clock_4_out), .T(T), .Q(Q_9), .Qn(nQ_9));  // open: preset, reset, en
  Clock clock_5 (.out(clock_5_out));
  Clock clock_6 (.out(clock_6_out));
  Clock clock_7 (.out(clock_7_out));
  Clock clock_8 (.out(clock_8_out));
  S_R_Flip_Flop #(.trigger("falling")) SR_F_F_Falling (
    .S(S_4), .clk(clock_5_out), .R(R_4), .Q(Q_4), .Qn(nQ_4));  // open: preset, reset, en
  D_Flip_Flop #(.trigger("falling")) D_F_F_Falling (
    .clk(clock_6_out), .D(D), .Q(Q_5), .Qn(nQ_5));  // open: preset, en, reset
  J_K_Flip_Flop #(.trigger("falling")) JK_F_F_Falling (
    .J(J_2), .clk(clock_7_out), .K(K_2), .Q(Q_8), .Qn(nQ_8));  // open: preset, en, reset
  T_Flip_Flop #(.trigger("falling")) T_F_F_Falling (
    .clk(clock_8_out), .T(T_2), .Q(Q_10), .Qn(nQ_10));  // open: preset, reset, en
  nand nand_1 (nand_1_out, S, Enable);
  nand nand_2 (nand_2_out, Enable, R_2);
  nand nand_3 (Q_2, nand_1_out, nQ);
  nand nand_4 (nQ, Q_2, nand_2_out);

  // Notes on the sheet:
  //   NOR Gate SR Latch
  //   Gated SR Latch
endmodule
